// Logisim project main.circ as structural Verilog
module ALU (
  input  [7:0] Data,
  input  [3:0] Control,
  input  Clk,
  output [7:0] DOUT,
  output [2:0] COZ
);

  wire [7:0] adder_1_out, register_1_q, register_2_q, subtractor_1_out;

  Register register_1 (.D(Data), .en(Control[0]), .clk(Clk), .Q(register_1_q));  // open: clr
  Register register_2 (.D(Data), .en(Control[1]), .clk(Clk), .Q(register_2_q));  // open: clr
  Adder adder_1 (.a(register_1_q), .b(register_2_q), .out(adder_1_out), .cout(COZ[0]));  // open: cin
  Subtractor subtractor_1 (.a(register_1_q), .b(register_2_q), .out(subtractor_1_out), .bout(COZ[1]));  // open: bin
  assign {DOUT[7:6], DOUT[6], DOUT[4:0]} = Control[2] ? adder_1_out : 8'bz;  // Controlled_Buffer controlled_buffer_1
  assign {DOUT[7:6], DOUT[6], DOUT[4:0]} = Control[3] ? subtractor_1_out : 8'bz;  // Controlled_Buffer controlled_buffer_2
  and and_1 (COZ[2], ~DOUT[0], ~DOUT[1], ~DOUT[2], ~DOUT[3], ~DOUT[4], ~DOUT[6], ~DOUT[6], ~DOUT[7]);  // AND_Gate

  assign DOUT[5] = DOUT[6];
endmodule

module RegBlock (
  input  [7:0] Data,
  input  [3:0] Control,
  input  Clk,
  output [7:0] Dout
);

  wire [7:0] register_1_q, register_2_q;

  Register register_1 (.D(Data), .en(Control[0]), .clk(Clk), .Q(register_1_q));  // open: clr
  Register register_2 (.D(Data), .en(Control[1]), .clk(Clk), .Q(register_2_q));  // open: clr
  assign Dout = Control[3] ? register_2_q : 8'bz;  // Controlled_Buffer controlled_buffer_1
  assign Dout = Control[2] ? register_1_q : 8'bz;  // Controlled_Buffer controlled_buffer_2
endmodule

module CavemansCore (
  input  [7:0] in_1,
  input  in_2,
  output [7:0] out_3
);

  wire clock_1_out, controlunit_1_io, controlunit_1_ioenabled, not_1_out;
  wire [3:0] controlunit_1_control_alu, controlunit_1_control_regblock;
  wire [15:0] controlunit_1_address;

  Clock clock_1 (.out(clock_1_out));
  RAM #(.addrWidth(16)) ram_1 (
    .addr(controlunit_1_address), .we(not_1_out), .oe(controlunit_1_ioenabled), .clk(clock_1_out),
    .din(in_1), .dout(in_1));
  not not_1 (not_1_out, controlunit_1_io);
  ControlUnit controlunit_1 (
    .Data(in_1), .Clk(clock_1_out), .Reset(in_2), .address(controlunit_1_address), .DOUT(in_1),
    .Control_Regblock(controlunit_1_control_regblock), .Control_ALU(controlunit_1_control_alu),
    .IO(controlunit_1_io), .ioenabled(controlunit_1_ioenabled));  // open: Int, BS
  RegBlock regblock_1 (.Data(in_1), .Control(controlunit_1_control_regblock), .Clk(clock_1_out), .Dout(in_1));
  ALU alu_1 (.Data(in_1), .Control(controlunit_1_control_alu), .Clk(clock_1_out), .DOUT(in_1));  // open: COZ

  assign out_3 = in_1;
endmodule

module ControlUnit (
  input  [7:0] Data,
  input  Clk,
  input  Int,
  input  Reset,
  output [15:0] address,
  output [7:0] DOUT,
  output [3:0] Control_Regblock,
  output [3:0] Control_ALU,
  output BS,
  output IO,
  output ioenabled
);

  wire and_1_out, and_2_out, and_3_out, and_4_out, and_5_out, and_6_out, and_7_out, and_8_out, and_9_out,
       and_10_out, and_11_out, controlled_buffer_9_out, controlled_buffer_10_out, controlled_buffer_12_out,
       controlled_buffer_13_out, not_1_out, shift_register_1_p4, shift_register_1_p6, shift_register_1_p12,
       shift_register_1_p13, shift_register_1_p14;
  wire [3:0] controlled_buffer_2_out;
  wire [6:0] controlled_buffer_3_out;
  wire [7:0] register_1_q;

  Register register_1 (.D(Data), .en(ioenabled), .clk(Clk), .Q(register_1_q), .clr(Reset));
  Counter #(.max('hffff), .width(16)) counter_1 (
    .count(controlled_buffer_13_out), .Q(address), .up(1'b1), .clk(Clk), .clr(Reset));  // open: load, D, carry
  // Shift_Register #(.length(5)) shift_register_1: pin names not known; wires that end beside it: Clk, Int, ioenabled, shift_register_1_p4, Clk, shift_register_1_p6, 1'b1, 1'b0, 1'b0, 1'b0, 1'b0, shift_register_1_p12, shift_register_1_p13, shift_register_1_p14
  buf buffer_1 (shift_register_1_p4, Reset);
  and and_1 (and_1_out, ~register_1_q[0], ~register_1_q[2], ~register_1_q[4], ~register_1_q[6]);  // AND_Gate
  and and_2 (and_2_out, register_1_q[0], ~register_1_q[2], ~register_1_q[4], ~register_1_q[6]);  // AND_Gate
  buf buffer_2 (shift_register_1_p4, controlled_buffer_12_out);
  and and_3 (and_3_out, and_1_out, shift_register_1_p12);
  and and_4 (and_4_out, ~register_1_q[4], register_1_q[5], and_3_out);  // AND_Gate
  and and_5 (and_5_out, ~register_1_q[4], ~register_1_q[5], and_3_out);  // AND_Gate
  assign controlled_buffer_3_out[1] = and_3_out ? and_4_out : 1'bz;  // Controlled_Buffer controlled_buffer_1
  assign {controlled_buffer_3_out[6:4], controlled_buffer_2_out[3], controlled_buffer_3_out[3], controlled_buffer_2_out[1:0]} = and_3_out ? {7{1'b0}} : 7'bz;  // Controlled_Buffer controlled_buffer_2
  assign controlled_buffer_3_out[0] = and_3_out ? and_5_out : 1'bz;  // Controlled_Buffer controlled_buffer_3
  buf buffer_3 (controlled_buffer_3_out[2], and_3_out);
  and and_6 (and_6_out, and_1_out, shift_register_1_p13);
  and and_7 (and_7_out, ~register_1_q[6], register_1_q[7], and_6_out);  // AND_Gate
  and and_8 (and_8_out, ~register_1_q[6], ~register_1_q[7], and_6_out);  // AND_Gate
  assign controlled_buffer_3_out[0] = and_6_out ? and_8_out : 1'bz;  // Controlled_Buffer controlled_buffer_4
  assign controlled_buffer_3_out[1] = and_6_out ? and_7_out : 1'bz;  // Controlled_Buffer controlled_buffer_5
  assign {controlled_buffer_3_out[6:4], controlled_buffer_2_out[3], controlled_buffer_3_out[2], controlled_buffer_2_out[1:0]} = and_6_out ? {7{1'b0}} : 7'bz;  // Controlled_Buffer controlled_buffer_6
  buf buffer_4 (controlled_buffer_3_out[3], and_6_out);
  and and_9 (and_9_out, and_1_out, shift_register_1_p14);
  and and_10 (and_10_out, ~register_1_q[4], ~register_1_q[5], and_9_out);  // AND_Gate
  and and_11 (and_11_out, ~register_1_q[4], register_1_q[5], and_9_out);  // AND_Gate
  assign controlled_buffer_2_out[0] = and_9_out ? and_10_out : 1'bz;  // Controlled_Buffer controlled_buffer_7
  assign controlled_buffer_2_out[1] = and_9_out ? and_11_out : 1'bz;  // Controlled_Buffer controlled_buffer_8
  buf buffer_5 (controlled_buffer_2_out[3], and_9_out);
  assign controlled_buffer_9_out = and_1_out ? and_9_out : 1'bz;  // Controlled_Buffer controlled_buffer_9
  assign controlled_buffer_10_out = and_1_out ? and_9_out : 1'bz;  // Controlled_Buffer controlled_buffer_10
  assign controlled_buffer_3_out = and_9_out ? {7{1'b0}} : 7'bz;  // Controlled_Buffer controlled_buffer_11
  assign controlled_buffer_12_out = ioenabled ? 1'b0 : 1'bz;  // Controlled_Buffer controlled_buffer_12
  assign controlled_buffer_13_out = ioenabled ? 1'b0 : 1'bz;  // Controlled_Buffer controlled_buffer_13
  assign controlled_buffer_12_out = not_1_out ? controlled_buffer_9_out : 1'bz;  // Controlled_Buffer controlled_buffer_14
  assign controlled_buffer_13_out = not_1_out ? controlled_buffer_10_out : 1'bz;  // Controlled_Buffer controlled_buffer_15
  assign {IO, BS, Control_ALU, Control_Regblock} = ioenabled ? 10'h200 : 10'bz;  // Controlled_Buffer controlled_buffer_16
  not not_1 (not_1_out, ioenabled);
  assign {IO, BS, Control_ALU, Control_Regblock} = not_1_out ? {controlled_buffer_3_out[6:4], controlled_buffer_2_out[3], controlled_buffer_3_out[3:0], controlled_buffer_2_out[1:0]} : 10'bz;  // Controlled_Buffer controlled_buffer_17

  // Notes on the sheet:
  //   buffer_1 drives only 1 and floats otherwise
  //   buffer_2 drives only 1 and floats otherwise
  //   buffer_3 drives only 1 and floats otherwise
  //   buffer_4 drives only 1 and floats otherwise
  //   buffer_5 drives only 1 and floats otherwise
endmodule
